// Logisim project Datapath.circ as structural Verilog: 13 circuits, main circuit 1-Bit-ALU main Circuit
module _1_Bit_ALU_main_Circuit (
  input  Input_B,
  input  Input_A,
  input  cin,
  input  [1:0] Selector,
  input  Binv,
  output Result,
  output cout
);

  wire adder_1_out, and_1_out, multiplexer_1_out, not_1_out, or_1_out, xor_1_out;

  Multiplexer multiplexer_1 (.in0(Input_A), .in1(not_1_out), .out(multiplexer_1_out), .sel(Binv));  // open: en
  not not_1 (not_1_out, Input_A);
  and and_1 (and_1_out, Input_B, Input_A);
  or or_1 (or_1_out, Input_B, Input_A);
  xor xor_1 (xor_1_out, Input_B, Input_A);
  Adder #(.width(1)) adder_1 (.a(Input_B), .b(multiplexer_1_out), .out(adder_1_out), .cin(cin), .cout(cout));
  Multiplexer #(.select(2)) multiplexer_2 (
    .in0(adder_1_out), .in1(and_1_out), .in2(or_1_out), .in3(xor_1_out), .out(Result), .sel(Selector));  // open: en
endmodule

module _1_Bit_ALU (
  input  Cin,
  input  Input_A,
  input  Input_B,
  input  [1:0] Selector,
  input  Binv,
  output Resut,
  output Cout
);

  _1_Bit_ALU_main_Circuit u_1_bit_alu_main_circuit_1 (
    .Result(Resut), .cout(Cout), .Input_B(Input_A), .Input_A(Input_B), .cin(Cin), .Binv(Binv),
    .Selector(Selector));
endmodule

module _12_Bit_ALU_main_circuit (
  input  [11:0] Input_A,
  input  [11:0] Input_A_2,
  input  ciin,
  input  Binv,
  input  [3:0] in_5,
  output Zero_Signal,
  output [11:0] Result,
  output Cout
);

  wire n1_bit_alu_1_cout, n1_bit_alu_2_cout, n1_bit_alu_3_cout, n1_bit_alu_4_cout, n1_bit_alu_5_cout,
       n1_bit_alu_6_cout, n1_bit_alu_7_cout, n1_bit_alu_8_cout, n1_bit_alu_9_cout, n1_bit_alu_10_cout,
       n1_bit_alu_11_cout, or_1_out;
  wire [11:0] n1_bit_alu_1_resut, shifter_1_result;

  _1_Bit_ALU u_1_bit_alu_1 (
    .Input_A(Input_A[0]), .Input_B(Input_A_2[0]), .Cin(ciin), .Binv(Binv), .Selector(in_5[1:0]),
    .Resut(n1_bit_alu_1_resut[0]), .Cout(n1_bit_alu_1_cout));
  _1_Bit_ALU u_1_bit_alu_2 (
    .Input_A(Input_A[1]), .Input_B(Input_A_2[1]), .Cin(n1_bit_alu_1_cout), .Binv(Binv), .Selector(in_5[1:0]),
    .Resut(n1_bit_alu_1_resut[1]), .Cout(n1_bit_alu_2_cout));
  _1_Bit_ALU u_1_bit_alu_3 (
    .Input_A(Input_A[2]), .Input_B(Input_A_2[2]), .Cin(n1_bit_alu_2_cout), .Binv(Binv), .Selector(in_5[1:0]),
    .Resut(n1_bit_alu_1_resut[2]), .Cout(n1_bit_alu_3_cout));
  _1_Bit_ALU u_1_bit_alu_4 (
    .Input_A(Input_A[3]), .Input_B(Input_A_2[3]), .Cin(n1_bit_alu_3_cout), .Binv(Binv), .Selector(in_5[1:0]),
    .Resut(n1_bit_alu_1_resut[3]), .Cout(n1_bit_alu_4_cout));
  _1_Bit_ALU u_1_bit_alu_5 (
    .Input_A(Input_A[4]), .Input_B(Input_A_2[4]), .Cin(n1_bit_alu_4_cout), .Binv(Binv), .Selector(in_5[1:0]),
    .Resut(n1_bit_alu_1_resut[4]), .Cout(n1_bit_alu_5_cout));
  _1_Bit_ALU u_1_bit_alu_6 (
    .Input_A(Input_A[5]), .Input_B(Input_A_2[5]), .Cin(n1_bit_alu_5_cout), .Binv(Binv), .Selector(in_5[1:0]),
    .Resut(n1_bit_alu_1_resut[5]), .Cout(n1_bit_alu_6_cout));
  _1_Bit_ALU u_1_bit_alu_7 (
    .Input_A(Input_A[6]), .Input_B(Input_A_2[6]), .Cin(n1_bit_alu_6_cout), .Binv(Binv), .Selector(in_5[1:0]),
    .Resut(n1_bit_alu_1_resut[6]), .Cout(n1_bit_alu_7_cout));
  _1_Bit_ALU u_1_bit_alu_8 (
    .Input_A(Input_A[7]), .Input_B(Input_A_2[7]), .Cin(n1_bit_alu_7_cout), .Binv(Binv), .Selector(in_5[1:0]),
    .Resut(n1_bit_alu_1_resut[7]), .Cout(n1_bit_alu_8_cout));
  _1_Bit_ALU u_1_bit_alu_9 (
    .Input_A(Input_A[8]), .Input_B(Input_A_2[8]), .Cin(n1_bit_alu_8_cout), .Binv(Binv), .Selector(in_5[1:0]),
    .Resut(n1_bit_alu_1_resut[8]), .Cout(n1_bit_alu_9_cout));
  _1_Bit_ALU u_1_bit_alu_10 (
    .Input_A(Input_A[9]), .Input_B(Input_A_2[9]), .Cin(n1_bit_alu_9_cout), .Binv(Binv), .Selector(in_5[1:0]),
    .Resut(n1_bit_alu_1_resut[9]), .Cout(n1_bit_alu_10_cout));
  _1_Bit_ALU u_1_bit_alu_11 (
    .Input_A(Input_A[10]), .Input_B(Input_A_2[10]), .Cin(n1_bit_alu_10_cout), .Binv(Binv),
    .Selector(in_5[1:0]), .Resut(n1_bit_alu_1_resut[10]), .Cout(n1_bit_alu_11_cout));
  _1_Bit_ALU u_1_bit_alu_12 (
    .Input_A(Input_A[11]), .Input_B(Input_A_2[11]), .Cin(n1_bit_alu_11_cout), .Binv(Binv),
    .Selector(in_5[1:0]), .Resut(n1_bit_alu_1_resut[11]), .Cout(Cout));
  Shifter shifter_1 (.Input(Input_A), .Shift_ammunt(Input_A_2[1:0]), .Shift_type(in_5[3]), .Result(shifter_1_result));
  or or_1 (or_1_out, n1_bit_alu_1_resut[0], n1_bit_alu_1_resut[1], n1_bit_alu_1_resut[2], n1_bit_alu_1_resut[3], n1_bit_alu_1_resut[4], n1_bit_alu_1_resut[5], n1_bit_alu_1_resut[6], n1_bit_alu_1_resut[7], n1_bit_alu_1_resut[8], n1_bit_alu_1_resut[9], n1_bit_alu_1_resut[10], n1_bit_alu_1_resut[11]);
  not not_1 (Zero_Signal, or_1_out);
  Multiplexer #(.width(12)) multiplexer_1 (
    .in0(n1_bit_alu_1_resut), .in1(shifter_1_result), .out(Result), .sel(in_5[2]));  // open: en

  // Notes on the sheet:
  //   Select bit
  //   Shift type
  //   Shift
endmodule

// Regidter File
module Register_File_main_circuit (
  input  [11:0] Data,
  input  Reg_write,
  input  [1:0] RS,
  input  [1:0] RD,
  input  [1:0] RT,
  input  Clock,
  output [11:0] RS_Data,
  output [11:0] RT_Data
);

  wire and_1_out, and_2_out, and_3_out, and_4_out, decoder_1_out0, decoder_1_out1, decoder_1_out2,
       decoder_1_out3;
  wire [11:0] R0_q, R1_q, R2_q, R3_q;

  Decoder #(.select(2)) decoder_1 (
    .out0(decoder_1_out0), .out1(decoder_1_out1), .out2(decoder_1_out2), .out3(decoder_1_out3), .sel(RD));  // open: en
  and and_1 (and_1_out, Reg_write, decoder_1_out0);
  and and_2 (and_2_out, Reg_write, decoder_1_out1);
  and and_3 (and_3_out, Reg_write, decoder_1_out2);
  and and_4 (and_4_out, Reg_write, decoder_1_out3);
  Register #(.width(12)) R0 (.D(Data), .en(and_1_out), .Q(R0_q), .clk(Clock));  // open: clr
  Register #(.width(12)) R1 (.D(Data), .en(and_2_out), .Q(R1_q), .clk(Clock));  // open: clr
  Register #(.width(12)) R2 (.D(Data), .en(and_3_out), .Q(R2_q), .clk(Clock));  // open: clr
  Register #(.width(12)) R3 (.D(Data), .en(and_4_out), .Q(R3_q), .clk(Clock));  // open: clr
  Multiplexer #(.select(2), .width(12)) multiplexer_1 (
    .in0(R0_q), .in1(R1_q), .in2(R2_q), .in3(R3_q), .out(RS_Data), .sel(RS));  // open: en
  Multiplexer #(.select(2), .width(12)) multiplexer_2 (
    .in0(R0_q), .in1(R1_q), .in2(R2_q), .in3(R3_q), .out(RT_Data), .sel(RT));  // open: en
endmodule

module Data_path (
  input  in_1,
  output [11:0] Result,
  output Cout
);

  wire and_1_out, clock_1_out, control_unit_1_alusrc, control_unit_1_binv, control_unit_1_branch,
       control_unit_1_branch_bne, control_unit_1_cin, control_unit_1_jump, control_unit_1_memread,
       control_unit_1_memtoreg, control_unit_1_memwrite, control_unit_1_regdest, control_unit_1_regwrite,
       multiplexer_4_out, n12_bit_alu_1_zero_bit;
  wire [1:0] multiplexer_1_out;
  wire [3:0] alu_contol_1_out_2;
  wire [7:0] rom_1_data;
  wire [11:0] adder_1_out, adder_2_out, bit_extender_1_out, bit_extender_2_out, multiplexer_2_out,
       multiplexer_3_out, multiplexer_5_out, multiplexer_6_out, ram_1_data, register_1_q,
       register_file_1_rs_data, register_file_1_rt_data;
  wire [11:8] rom_1_data_2;

  Clock clock_1 (.out(clock_1_out));
  Adder #(.width(12)) adder_1 (.a(12'h1), .b(register_1_q), .out(adder_1_out));  // open: cin, cout
  Register #(.width(12)) register_1 (
    .D(multiplexer_6_out), .Q(register_1_q), .clk(clock_1_out), .clr(in_1));  // open: en
  assign bit_extender_1_out = {{4{1'b0}}, rom_1_data};  // Bit_Extender bit_extender_1
  ROM #(.addrWidth(12), .dataWidth(12)) rom_1 (.addr(register_1_q), .data({rom_1_data_2, rom_1_data}));  // open: sel
  Control_unit control_unit_1 (
    .in_1(rom_1_data_2), .RegDest(control_unit_1_regdest), .RegWrite(control_unit_1_regwrite),
    .ALUsrc(control_unit_1_alusrc), .Binv(control_unit_1_binv), .Cin(control_unit_1_cin),
    .MemToReg(control_unit_1_memtoreg), .Branch(control_unit_1_branch),
    .Branch_Bne(control_unit_1_branch_bne), .Jump(control_unit_1_jump), .MemWrite(control_unit_1_memwrite),
    .MemRead(control_unit_1_memread));
  assign bit_extender_2_out = {{8{1'b0}}, rom_1_data[3:0]};  // Bit_Extender bit_extender_2
  Multiplexer #(.width(2)) multiplexer_1 (
    .in0(rom_1_data[3:2]), .in1(rom_1_data[7:6]), .out(multiplexer_1_out), .sel(control_unit_1_regdest));  // open: en
  Register_File register_file_1 (
    .RT(multiplexer_1_out), .RS(rom_1_data[5:4]), .RD(rom_1_data[7:6]), .Data(multiplexer_5_out),
    .clock(clock_1_out), .regWrite(control_unit_1_regwrite), .RS_Data(register_file_1_rs_data),
    .RT_Data(register_file_1_rt_data));
  _12_Bit_ALU u_12_bit_alu_1 (
    .Input_A(register_file_1_rs_data), .Input_B(multiplexer_2_out), .Cin(control_unit_1_cin),
    .Binv(control_unit_1_binv), .Select_Bit__shift(alu_contol_1_out_2), .Zero_Bit(n12_bit_alu_1_zero_bit),
    .Result(Result), .Cout(Cout));
  Multiplexer #(.width(12)) multiplexer_2 (
    .in0(register_file_1_rt_data), .in1(bit_extender_2_out), .out(multiplexer_2_out),
    .sel(control_unit_1_alusrc));  // open: en
  Alu_Contol alu_contol_1 (.in_1(rom_1_data_2), .out_2(alu_contol_1_out_2));
  Multiplexer #(.width(12)) multiplexer_3 (
    .in0(adder_1_out), .in1(adder_2_out), .out(multiplexer_3_out), .sel(and_1_out));  // open: en
  Adder #(.width(12)) adder_2 (.a(adder_1_out), .b(bit_extender_2_out), .out(adder_2_out));  // open: cin, cout
  and and_1 (and_1_out, control_unit_1_branch, multiplexer_4_out);
  Multiplexer multiplexer_4 (
    .in0(n12_bit_alu_1_zero_bit), .in1(1'b1), .out(multiplexer_4_out), .sel(control_unit_1_branch_bne));  // open: en
  Multiplexer #(.width(12)) multiplexer_5 (
    .in0(Result), .in1(ram_1_data), .out(multiplexer_5_out), .sel(control_unit_1_memtoreg));  // open: en
  Multiplexer #(.width(12)) multiplexer_6 (
    .in0(multiplexer_3_out), .in1(bit_extender_1_out), .out(multiplexer_6_out), .sel(control_unit_1_jump));  // open: en
  RAM #(.addrWidth(12), .dataWidth(12), .bus("separate")) ram_1 (
    .addr(Result), .din(register_file_1_rt_data), .data(ram_1_data), .str(control_unit_1_memwrite),
    .clk(clock_1_out), .ld(control_unit_1_memread));  // open: sel, clr

  // Notes on the sheet:
  //   contents of rom_1 (hex, n*v repeats v):
  //   a13 9a1 901 c00
  //   Zero Bit
endmodule

// ALU
module _12_Bit_ALU (
  input  Cin,
  input  [11:0] Input_A,
  input  [11:0] Input_B,
  input  Binv,
  input  [3:0] Select_Bit__shift,
  output Zero_Bit,
  output [11:0] Result,
  output Cout
);

  _12_Bit_ALU_main_circuit u_12_bit_alu_main_circuit_1 (
    .Result(Result), .Cout(Cout), .Input_A(Input_A), .Input_A_2(Input_B), .ciin(Cin), .Binv(Binv),
    .Zero_Signal(Zero_Bit), .in_5(Select_Bit__shift));
endmodule

// Reg file
module Register_File (
  input  [1:0] RT,
  input  [1:0] RS,
  input  [1:0] RD,
  input  [11:0] Data,
  input  regWrite,
  input  clock,
  output [11:0] RS_Data,
  output [11:0] RT_Data
);

  Register_File_main_circuit register_file_main_circuit_1 (
    .Data(Data), .Reg_write(regWrite), .Clock(clock), .RS_Data(RS_Data), .RT_Data(RT_Data), .RD(RD), .RS(RS),
    .RT(RT));
endmodule

module Shifter_Circuit (
  input  [11:0] Input,
  input  [1:0] Shift_Ammount,
  input  Shift_type,
  output [11:0] Result
);

  wire [3:0] bit_extender_1_out;
  wire [11:0] shifter_1_out, shifter_2_out;

  assign bit_extender_1_out = {{2{1'b0}}, Shift_Ammount};  // Bit_Extender bit_extender_1
  Shifter_part #(.width(12)) shifter_1 (.in(Input), .\dist (bit_extender_1_out), .out(shifter_1_out));
  Shifter_part #(.width(12), .shift("lr")) shifter_2 (.in(Input), .\dist (bit_extender_1_out), .out(shifter_2_out));
  Multiplexer #(.width(12)) multiplexer_1 (
    .in0(shifter_1_out), .in1(shifter_2_out), .out(Result), .sel(Shift_type));  // open: en
endmodule

module Shifter (
  input  [11:0] Input,
  input  [1:0] Shift_ammunt,
  input  Shift_type,
  output [11:0] Result
);

  Shifter_Circuit shifter_circuit_1 (
    .Input(Input), .Shift_Ammount(Shift_ammunt), .Shift_type(Shift_type), .Result(Result));
endmodule

module Control_Unit_Circuit (
  input  Input3,
  input  Input2,
  input  Input1,
  input  Input0,
  output RegDest,
  output RegWrite,
  output ALUsrc,
  output Binv,
  output Cin,
  output MemToReg,
  output Branch,
  output BranchBne,
  output Jump,
  output MemWrite,
  output MemRead
);

  wire and_1_out, and_2_out, and_3_out, and_4_out, and_5_out, and_6_out, and_7_out, and_8_out, and_9_out,
       and_10_out, and_11_out, and_12_out, and_13_out, and_14_out, and_15_out, and_16_out, and_17_out,
       and_18_out, and_19_out, and_20_out, and_21_out, and_22_out, and_23_out, and_24_out, and_31_out,
       not_1_out, not_2_out, not_3_out, not_4_out, not_5_out, not_6_out, not_7_out, not_8_out, not_9_out,
       not_10_out, not_11_out, not_12_out, not_13_out, not_14_out, not_15_out, not_16_out, not_17_out,
       not_18_out, not_19_out, not_20_out, or_3_out;

  and and_1 (and_1_out, Input3, not_1_out);
  not not_1 (not_1_out, Input0);
  and and_2 (and_2_out, Input3, Input1);
  not not_2 (not_2_out, Input3);
  not not_3 (not_3_out, Input1);
  and and_3 (and_3_out, not_3_out, Input0);
  not not_4 (not_4_out, Input3);
  and and_4 (and_4_out, not_4_out, not_5_out);
  not not_5 (not_5_out, Input2);
  not not_6 (not_6_out, Input3);
  and and_5 (and_5_out, not_6_out, Input1);
  not not_7 (not_7_out, Input3);
  and and_6 (and_6_out, not_7_out, not_8_out);
  not not_8 (not_8_out, Input2);
  not not_9 (not_9_out, Input1);
  and and_7 (and_7_out, not_9_out, Input0);
  not not_10 (not_10_out, Input3);
  and and_8 (and_8_out, not_10_out, not_11_out);
  not not_11 (not_11_out, Input2);
  not not_12 (not_12_out, Input1);
  and and_9 (and_9_out, not_12_out, Input0);
  and and_10 (and_10_out, Input2, Input1);
  and and_11 (and_11_out, Input3, not_13_out);
  not not_13 (not_13_out, Input2);
  and and_12 (and_12_out, Input3, not_14_out);
  not not_14 (not_14_out, Input2);
  and and_13 (and_13_out, Input1, Input0);
  and and_14 (and_14_out, Input3, Input2);
  not not_15 (not_15_out, Input1);
  and and_15 (and_15_out, not_15_out, not_16_out);
  not not_16 (not_16_out, Input0);
  and and_16 (and_16_out, Input3, not_17_out);
  not not_17 (not_17_out, Input2);
  not not_18 (not_18_out, Input1);
  and and_17 (and_17_out, not_18_out, not_19_out);
  not not_19 (not_19_out, Input0);
  and and_18 (and_18_out, Input2, Input1);
  or or_1 (RegDest, and_1_out, and_2_out);
  or or_2 (RegWrite, not_2_out, and_3_out);
  and and_19 (and_19_out, and_4_out, Input1);
  and and_20 (and_20_out, and_5_out, Input0);
  not not_20 (not_20_out, Input1);
  and and_21 (and_21_out, and_6_out, and_7_out);
  and and_22 (and_22_out, Input3, Input1);
  and and_23 (and_23_out, and_8_out, and_9_out);
  and and_24 (and_24_out, Input3, Input1);
  and and_25 (MemToReg, and_10_out, Input0);
  and and_26 (Branch, and_11_out, Input1);
  and and_27 (BranchBne, and_12_out, and_13_out);
  and and_28 (Jump, and_14_out, and_15_out);
  and and_29 (MemWrite, and_16_out, and_17_out);
  and and_30 (MemRead, and_18_out, Input0);
  or or_3 (or_3_out, and_19_out, and_20_out);
  and and_31 (and_31_out, Input3, not_20_out);
  or or_4 (Binv, and_21_out, and_22_out);
  or or_5 (Cin, and_23_out, and_24_out);
  or or_6 (ALUsrc, or_3_out, and_31_out);
endmodule

module ALU_Control_Circuit (
  input  Input0,
  input  Input1,
  input  Input2,
  input  input3,
  output ShiftType,
  output Shift,
  output selectBit1,
  output selectBit0
);

  wire and_1_out, and_2_out, and_3_out, and_4_out, and_5_out, and_6_out, and_7_out, and_10_out, and_11_out,
       and_12_out, and_13_out, not_1_out, not_2_out, not_3_out, not_4_out, not_5_out, not_6_out, not_7_out,
       not_8_out, or_2_out;

  not not_1 (not_1_out, input3);
  and and_1 (and_1_out, not_1_out, not_2_out);
  not not_2 (not_2_out, Input2);
  and and_2 (and_2_out, Input1, Input0);
  not not_3 (not_3_out, input3);
  and and_3 (and_3_out, not_3_out, not_4_out);
  not not_4 (not_4_out, Input2);
  and and_4 (and_4_out, Input2, not_5_out);
  not not_5 (not_5_out, Input1);
  and and_5 (and_5_out, Input2, Input1);
  not not_6 (not_6_out, Input0);
  and and_6 (and_6_out, Input2, not_7_out);
  not not_7 (not_7_out, Input0);
  and and_7 (and_7_out, input3, Input2);
  and and_8 (ShiftType, and_1_out, and_2_out);
  and and_9 (Shift, and_3_out, Input1);
  and and_10 (and_10_out, and_4_out, Input0);
  and and_11 (and_11_out, and_5_out, not_6_out);
  and and_12 (and_12_out, input3, Input2);
  not not_8 (not_8_out, Input1);
  or or_1 (selectBit0, and_6_out, and_7_out);
  or or_2 (or_2_out, and_10_out, and_11_out);
  and and_13 (and_13_out, and_12_out, not_8_out);
  or or_3 (selectBit1, or_2_out, and_13_out);
endmodule

module Alu_Contol (
  input  [3:0] in_1,
  output [3:0] out_2
);

  ALU_Control_Circuit alu_control_circuit_1 (
    .Input0(in_1[0]), .Input1(in_1[1]), .Input2(in_1[2]), .input3(in_1[3]), .ShiftType(out_2[3]),
    .Shift(out_2[2]), .selectBit1(out_2[1]), .selectBit0(out_2[0]));
endmodule

module Control_unit (
  input  [3:0] in_1,
  output RegDest,
  output RegWrite,
  output ALUsrc,
  output Binv,
  output Cin,
  output MemToReg,
  output Branch,
  output Branch_Bne,
  output Jump,
  output MemWrite,
  output MemRead
);

  Control_Unit_Circuit control_unit_circuit_1 (
    .Input3(in_1[3]), .Input2(in_1[2]), .Input1(in_1[1]), .Input0(in_1[0]), .RegDest(RegDest),
    .RegWrite(RegWrite), .ALUsrc(ALUsrc), .Binv(Binv), .Cin(Cin), .MemToReg(MemToReg), .Branch(Branch),
    .BranchBne(Branch_Bne), .Jump(Jump), .MemWrite(MemWrite), .MemRead(MemRead));
endmodule
